// Logisim project Lab01.circ as structural Verilog: 1 circuit, main circuit main
module main (
  input  A,
  input  A_2,
  input  B,
  input  B_2,
  input  C,
  input  in_6,
  input  A_3,
  input  in_8,
  input  B_3,
  input  Clear_A,
  input  C_2,
  input  B_4,
  input  D,
  input  Preset_B,
  input  Clear_B,
  output C_3,
  output out_17,
  output D_2,
  output A_output,
  output A_output_2,
  output B_output,
  output C_output,
  output D_output,
  output B_output_2
);

  wire and_1_out, and_2_out, and_3_out, and_4_out, clock_1_out, clock_2_out, nand_1_out, nor_1_out,
       not_1_out, not_2_out, not_3_out, not_4_out, xnor_1_out;

  Clock clock_1 (.out(clock_1_out));
  not not_1 (not_1_out, B);
  not not_2 (not_2_out, A);
  not not_3 (not_3_out, A);
  not not_4 (not_4_out, B);
  and and_1 (and_1_out, A, not_1_out);
  and and_2 (and_2_out, not_2_out, B);
  and and_3 (and_3_out, not_3_out, not_4_out);
  and and_4 (and_4_out, A, B);
  or or_1 (C_3, and_1_out, and_2_out);
  or or_2 (D_2, and_3_out, and_4_out);
  Register #(.width(4)) register_1 (
    .D({D, C_2, B_3, A_3}), .en(1'b1), .Q({D_output, C_output, B_output, A_output_2}), .clk(clock_1_out));  // open: clr
  Clock clock_2 (.out(clock_2_out));
  nor nor_1 (nor_1_out, A_2, B_2);
  nand nand_1 (nand_1_out, A_2, C);
  xnor xnor_1 (xnor_1_out, B_2, C);
  D_Flip_Flop d_ff_1 (
    .clk(clock_2_out), .D(in_6), .Q(A_output), .preset(in_8), .en(1'b1), .reset(Clear_A));  // open: Qn
  D_Flip_Flop d_ff_2 (
    .clk(clock_2_out), .D(B_4), .Q(B_output_2), .preset(Preset_B), .en(1'b1), .reset(Clear_B));  // open: Qn
  ExactlyOne xor_1 (.out(out_17), .in0(nor_1_out), .in2(nand_1_out), .in4(xnor_1_out));

  // Notes on the sheet:
  //   clock
  //   clock
  //   A
  //   Preset_A
  //   D_flip flop
  //   F
endmodule
